// Logisim project TP5.circ as structural Verilog: 17 circuits, main circuit TransicionJohnsonE1
module main (
);

  wire clock_1_out;
  wire [2:0] undriven, undriven_2;

  Clock clock_1 (.out(clock_1_out));
  LED led_1 (.in(undriven[0]));
  LED led_2 (.in(undriven[1]));
  LED led_3 (.in(undriven[2]));
  LED led_4 (.in(undriven_2[0]));
  LED led_5 (.in(undriven_2[1]));
  LED led_6 (.in(undriven_2[2]));
endmodule

module ContadorJohnsonE1 (
);

  wire clock_1_out, transicionjohnsone1_1_s0, transicionjohnsone1_1_s1, transicionjohnsone1_1_s2,
       transicionjohnsone1_1_s3;
  wire [3:0] counter_1_q;

  Clock clock_1 (.out(clock_1_out));
  Counter #(.max('h7), .width(4)) counter_1 (
    .Q(counter_1_q), .clk(clock_1_out));  // open: load, D, count, carry, up, clr
  TransicionJohnsonE1 transicionjohnsone1_1 (
    .C0(counter_1_q[0]), .C1(counter_1_q[1]), .C2(counter_1_q[2]), .C3(counter_1_q[3]),
    .S0(transicionjohnsone1_1_s0), .S1(transicionjohnsone1_1_s1), .S2(transicionjohnsone1_1_s2),
    .S3(transicionjohnsone1_1_s3));
  LedBar #(.matrixcols(4)) ledbar_1 (
    .led0(transicionjohnsone1_1_s3), .led1(transicionjohnsone1_1_s2), .led2(transicionjohnsone1_1_s1),
    .led3(transicionjohnsone1_1_s0));
  // Digital_Oscilloscope digital_oscilloscope_1: pin names not known; wires that end beside it: clock_1_out, transicionjohnsone1_1_s0, transicionjohnsone1_1_s1, transicionjohnsone1_1_s2, transicionjohnsone1_1_s3
endmodule

module TransicionJohnsonE1 (
  input  C0,
  input  C1,
  input  C2,
  input  C3,
  output S0,
  output S1,
  output S2,
  output S3
);

  wire and_1_out, and_2_out, and_3_out, and_4_out, and_5_out, and_6_out;

  and and_1 (and_1_out, ~C3, ~C2, C1);  // AND_Gate
  and and_2 (and_2_out, ~C3, C2, ~C1);  // AND_Gate
  and and_3 (and_3_out, ~C3, ~C2, C0);  // AND_Gate
  and and_4 (and_4_out, ~C3, C2, ~C1, ~C0);  // AND_Gate
  and and_5 (and_5_out, ~C3, ~C2, C1, C0);  // AND_Gate
  and and_6 (and_6_out, ~C3, C2, ~C0);  // AND_Gate
  and and_7 (S3, ~C3, C2);  // AND_Gate
  or or_1 (S1, and_1_out, and_2_out);
  or or_2 (S0, and_3_out, and_1_out, and_4_out);
  or or_3 (S2, and_2_out, and_5_out, and_6_out);
endmodule

module SecuenciadorBCDE2 (
);

  wire clock_1_out;
  wire [3:0] decodificarabcde2_1_bcd;
  wire [9:0] contadoranillo10bitse2_1_onehot;

  Clock clock_1 (.out(clock_1_out));
  ContadorAnillo10bitsE2 contadoranillo10bitse2_1 (.Clock(clock_1_out), .OneHot(contadoranillo10bitse2_1_onehot));
  Hex_Digit_Display hex_digit_display_1 (.value(decodificarabcde2_1_bcd));  // open: dp
  DecodificarABCDE2 decodificarabcde2_1 (.Entrada(contadoranillo10bitse2_1_onehot), .BCD(decodificarabcde2_1_bcd));
  LedBar #(.matrixcols(4)) ledbar_1 (
    .led0(decodificarabcde2_1_bcd[2]), .led1(decodificarabcde2_1_bcd[2]), .led2(decodificarabcde2_1_bcd[1]),
    .led3(decodificarabcde2_1_bcd[0]));
  // Digital_Oscilloscope digital_oscilloscope_1: pin names not known; wires that end beside it: clock_1_out, decodificarabcde2_1_bcd[0], decodificarabcde2_1_bcd[1], decodificarabcde2_1_bcd[2], decodificarabcde2_1_bcd[3]
endmodule

module ContadorAnillo10bitsE2 (
  input  Clock,
  output [9:0] OneHot
);

  wire por_1_out;

  POR por_1 (.out(por_1_out));
  D_Flip_Flop #(.trigger("falling")) d_ff_1 (
    .D(OneHot[0]), .clk(Clock), .Q(OneHot[9]), .preset(por_1_out));  // open: Qn, reset
  D_Flip_Flop #(.trigger("falling")) d_ff_2 (.D(OneHot[9]), .clk(Clock), .Q(OneHot[8]));  // open: Qn, preset, reset
  D_Flip_Flop #(.trigger("falling")) d_ff_3 (.D(OneHot[8]), .clk(Clock), .Q(OneHot[7]));  // open: Qn, preset, reset
  D_Flip_Flop #(.trigger("falling")) d_ff_4 (.D(OneHot[7]), .clk(Clock), .Q(OneHot[6]));  // open: Qn, preset, reset
  D_Flip_Flop #(.trigger("falling")) d_ff_5 (.D(OneHot[6]), .clk(Clock), .Q(OneHot[5]));  // open: Qn, preset, reset
  D_Flip_Flop #(.trigger("falling")) d_ff_6 (.D(OneHot[5]), .clk(Clock), .Q(OneHot[4]));  // open: Qn, preset, reset
  D_Flip_Flop #(.trigger("falling")) d_ff_7 (.D(OneHot[4]), .clk(Clock), .Q(OneHot[3]));  // open: Qn, preset, reset
  D_Flip_Flop #(.trigger("falling")) d_ff_8 (.D(OneHot[3]), .clk(Clock), .Q(OneHot[2]));  // open: Qn, preset, reset
  D_Flip_Flop #(.trigger("falling")) d_ff_9 (.D(OneHot[2]), .clk(Clock), .Q(OneHot[1]));  // open: Qn, preset, reset
  D_Flip_Flop #(.trigger("falling")) d_ff_10 (.D(OneHot[1]), .clk(Clock), .Q(OneHot[0]));  // open: Qn, preset, reset
endmodule

module DecodificarABCDE2 (
  input  [9:0] Entrada,
  output [3:0] BCD
);

  or or_1 (BCD[0], Entrada[0], Entrada[2], Entrada[4], Entrada[6], Entrada[8]);
  or or_2 (BCD[1], Entrada[1], Entrada[2], Entrada[5], Entrada[6]);
  or or_3 (BCD[2], Entrada[3], Entrada[4], Entrada[5], Entrada[6]);
  or or_4 (BCD[3], Entrada[7], Entrada[8]);

  // Other names for the same wires on the sheet: S0 = BCD[0]; S1 = BCD[1]; S2 = BCD[2]; S3 = BCD[3]; E0 = Entrada[0];
  //   E1 = Entrada[1]; E2 = Entrada[2]; E3 = Entrada[3]; E4 = Entrada[4]; E5 = Entrada[5]; E6 = Entrada[6];
  //   E7 = Entrada[7]; E8 = Entrada[8]; E9 = Entrada[9]
endmodule

module ContadorJohnson5BitsE3 (
);

  wire clock_1_out;
  wire [3:0] counter_1_q, digital_oscilloscope_1_p7;
  wire [4:0] transicionjohnsone3_1_s0;

  Clock clock_1 (.out(clock_1_out));
  Counter #(.max('h9), .width(4)) counter_1 (
    .Q(counter_1_q), .clk(clock_1_out));  // open: load, D, count, carry, up, clr
  TransicionJohnsonE3 transicionjohnsone3_1 (
    .C0(counter_1_q[0]), .C1(counter_1_q[1]), .C2(counter_1_q[2]), .C3(counter_1_q[3]),
    .S0(transicionjohnsone3_1_s0[0]), .S1(transicionjohnsone3_1_s0[1]), .S2(transicionjohnsone3_1_s0[2]),
    .S3(transicionjohnsone3_1_s0[3]), .S4(transicionjohnsone3_1_s0[4]));
  LedBar #(.matrixcols(5)) ledbar_1 (
    .led0(transicionjohnsone3_1_s0[4]), .led1(transicionjohnsone3_1_s0[3]),
    .led2(transicionjohnsone3_1_s0[2]), .led3(transicionjohnsone3_1_s0[1]), .led4(transicionjohnsone3_1_s0[0]));
  // Digital_Oscilloscope digital_oscilloscope_1: pin names not known; wires that end beside it: clock_1_out, transicionjohnsone3_1_s0[0], transicionjohnsone3_1_s0[1], transicionjohnsone3_1_s0[2], transicionjohnsone3_1_s0[3], transicionjohnsone3_1_s0[4], digital_oscilloscope_1_p7[0], digital_oscilloscope_1_p7[1], digital_oscilloscope_1_p7[2], digital_oscilloscope_1_p7[3]
  TransicionBCDAikenE3 transicionbcdaikene3_1 (.Johnson(transicionjohnsone3_1_s0), .Aiken(digital_oscilloscope_1_p7));
  LedBar #(.matrixcols(4)) ledbar_2 (
    .led0(digital_oscilloscope_1_p7[3]), .led1(digital_oscilloscope_1_p7[2]),
    .led2(digital_oscilloscope_1_p7[1]), .led3(digital_oscilloscope_1_p7[0]));
endmodule

module TransicionJohnsonE3 (
  input  C0,
  input  C1,
  input  C2,
  input  C3,
  output S0,
  output S1,
  output S2,
  output S3,
  output S4
);

  wire and_1_out, and_2_out, and_3_out, and_4_out, and_5_out, and_6_out, and_7_out, and_8_out, and_9_out,
       and_10_out, and_11_out, and_12_out, and_13_out;

  and and_1 (and_1_out, ~C3, ~C2, C0);  // AND_Gate
  and and_2 (and_2_out, ~C3, ~C2, C1);  // AND_Gate
  and and_3 (and_3_out, ~C3, C2, ~C1);  // AND_Gate
  and and_4 (and_4_out, ~C3, ~C2, C1);  // AND_Gate
  and and_5 (and_5_out, ~C3, C2, ~C1);  // AND_Gate
  and and_6 (and_6_out, ~C3, C1, ~C0);  // AND_Gate
  and and_7 (and_7_out, ~C3, C1, C0);  // AND_Gate
  and and_8 (and_8_out, ~C3, C2);  // AND_Gate
  and and_9 (and_9_out, C3, ~C2, ~C1, ~C0);  // AND_Gate
  and and_10 (and_10_out, ~C3, C2);  // AND_Gate
  and and_11 (and_11_out, ~C3, C2, C0);  // AND_Gate
  and and_12 (and_12_out, ~C3, C2, C1);  // AND_Gate
  and and_13 (and_13_out, C3, ~C2, ~C1);  // AND_Gate
  or or_1 (S0, and_1_out, and_2_out, and_3_out);
  or or_2 (S1, and_4_out, and_5_out, and_6_out);
  or or_3 (S2, and_7_out, and_8_out);
  or or_4 (S3, and_9_out, and_10_out);
  or or_5 (S4, and_11_out, and_12_out, and_13_out);
endmodule

module TransicionBCDAikenE3 (
  input  [4:0] Johnson,
  output [3:0] Aiken
);

  Multiplexer #(.select(5), .width(4)) multiplexer_1 (
    .in0(4'b0000), .in1(4'b0001), .in3(4'b0010), .in7(4'b0011), .in15(4'b0100), .in16(4'b1111),
    .in24(4'b1110), .in28(4'b1101), .in30(4'b1100), .in31(4'b1011), .out(Aiken), .sel(Johnson));  // open: in2, in4, in5, in6, in8, in9, in10, in11, in12, in13, in14, in17, in18, in19, in20, in21, in22, in23, in25, in26, in27, in29
endmodule

module PeriodicSignalGenE4 (
);

  wire clock_1_out, multiplexer_1_out;
  wire [2:0] counter_1_q, transicionjohnsone4_1_s0;

  Clock clock_1 (.out(clock_1_out));
  Counter #(.max('h5), .width(3)) counter_1 (
    .Q(counter_1_q), .clk(clock_1_out));  // open: load, D, count, carry, up, clr
  TransicionJohnsonE4 transicionjohnsone4_1 (
    .C0(counter_1_q[0]), .C1(counter_1_q[1]), .C2(counter_1_q[2]), .S0(transicionjohnsone4_1_s0[0]),
    .S1(transicionjohnsone4_1_s0[1]), .S2(transicionjohnsone4_1_s0[2]));
  LedBar #(.matrixcols(3)) ledbar_1 (
    .led0(transicionjohnsone4_1_s0[2]), .led1(transicionjohnsone4_1_s0[1]), .led2(transicionjohnsone4_1_s0[0]));
  Multiplexer #(.select(3)) multiplexer_1 (
    .in0(1'b1), .in1(1'b1), .in3(1'b0), .in4(1'b0), .in6(1'b0), .in7(1'b0), .out(multiplexer_1_out),
    .sel(transicionjohnsone4_1_s0));  // open: in2, in5
  // Digital_Oscilloscope digital_oscilloscope_1: pin names not known; wires that end beside it: clock_1_out, multiplexer_1_out
endmodule

module TransicionJohnsonE4 (
  input  C0,
  input  C1,
  input  C2,
  output S0,
  output S1,
  output S2
);

  wire and_1_out, and_2_out, and_3_out, and_4_out, and_5_out;

  and and_1 (and_1_out, C2, ~C1, ~C0);  // AND_Gate
  and and_2 (and_2_out, ~C2, C0);  // AND_Gate
  and and_3 (and_3_out, ~C1, C2);  // AND_Gate
  and and_4 (and_4_out, ~C2, C1);  // AND_Gate
  and and_5 (and_5_out, ~C2, C1, C0);  // AND_Gate
  or or_1 (S1, and_4_out, and_1_out);
  or or_2 (S0, and_4_out, and_2_out);
  or or_3 (S2, and_5_out, and_3_out);
endmodule

module FSME5 (
  input  A,
  output F
);

  wire and_1_out, and_2_out, and_3_out, and_4_out, and_5_out, and_6_out, Q0, Q1, S0, S1;

  and and_1 (and_1_out, ~S1, S0);  // AND_Gate
  and and_2 (and_2_out, S1, ~A);  // AND_Gate
  or or_1 (Q1, and_1_out, and_2_out);
  and and_3 (and_3_out, ~S0, A);  // AND_Gate
  and and_4 (and_4_out, ~S1, S0, ~A);  // AND_Gate
  and and_5 (and_5_out, S1, ~A);  // AND_Gate
  and and_6 (and_6_out, ~S1, S0, A);  // AND_Gate
  or or_2 (Q0, and_3_out, and_4_out);
  or or_3 (F, and_5_out, and_6_out);
  D_Flip_Flop #(.trigger("falling")) d_ff_1 (.D(Q1), .clk(A), .Q(S1));  // open: Qn, preset, reset
  D_Flip_Flop #(.trigger("falling")) d_ff_2 (.D(Q0), .clk(A), .Q(S0));  // open: Qn, preset, reset
endmodule

module FSME6 (
  input  A,
  output out_2
);

  wire and_1_out, and_2_out, and_3_out, and_4_out, and_5_out, Q0, Q1, S0, S1;

  and and_1 (and_1_out, S1, ~A);  // AND_Gate
  and and_2 (and_2_out, S1, ~S0);  // AND_Gate
  and and_3 (and_3_out, ~S1, S0, A);  // AND_Gate
  and and_4 (and_4_out, ~S0, A);  // AND_Gate
  and and_5 (and_5_out, ~S1, S0, ~A);  // AND_Gate
  or or_1 (out_2, S1, ~S0);  // OR_Gate
  or or_2 (Q1, and_1_out, and_2_out, and_3_out);
  or or_3 (Q0, and_4_out, and_5_out);
  D_Flip_Flop #(.trigger("falling")) d_ff_1 (.D(Q1), .clk(A), .Q(S1));  // open: Qn, preset, reset
  LED led_1 (.in(S1));
  LED led_2 (.in(S0));
  D_Flip_Flop #(.trigger("falling")) d_ff_2 (.D(Q0), .clk(A), .Q(S0));  // open: Qn, preset, reset

  // Other names for the same wires on the sheet: F = out_2
endmodule

module MaquinaDeGaseosasE7 (
  input  A1,
  input  A0,
  input  Reset,
  output G
);

  wire A0_t, A1_t, Clock, or_1_out, or_2_out, or_3_out, or_4_out, or_5_out, Q0, Q1, S0, S1;

  Clock clock_1 (.out(Clock));
  and and_1 (A1_t, A1, Clock);
  and and_2 (A0_t, Clock, A0);
  or or_1 (or_1_out, S1, S0, A1_t);
  or or_2 (or_2_out, S1, A1_t, A0_t);
  or or_3 (or_3_out, S1, S0, A0_t);
  or or_4 (or_4_out, S0, A1_t, A0_t);
  or or_5 (or_5_out, S1, ~S0, A1_t, ~A0_t);  // OR_Gate
  and and_3 (G, S1, S0);
  and and_4 (Q1, or_1_out, or_2_out);
  and and_5 (Q0, or_3_out, or_4_out, or_5_out);
  D_Flip_Flop #(.trigger("falling")) d_ff_1 (.D(Q1), .clk(Clock), .Q(S1), .reset(Reset));  // open: Qn, preset
  LED led_1 (.in(S1));
  LED led_2 (.in(S0));
  D_Flip_Flop #(.trigger("falling")) d_ff_2 (.D(Q0), .clk(Clock), .Q(S0), .reset(Reset));  // open: Qn, preset
endmodule

module ContadorBinarioSinc3BitsE8 (
);

  wire and_1_out, and_2_out, and_3_out, and_4_out, and_5_out, clock_1_out, Q0, Q1, Q2, S0, S1, S2;

  not not_1 (Q0, S0);
  and and_1 (and_1_out, ~S2, ~S1, ~S0);  // AND_Gate
  and and_2 (and_2_out, S2, S1);
  and and_3 (and_3_out, S2, S0);
  and and_4 (and_4_out, S0, S1);
  and and_5 (and_5_out, ~S0, ~S1);  // AND_Gate
  or or_1 (Q1, and_4_out, and_5_out);
  or or_2 (Q2, and_1_out, and_2_out, and_3_out);
  Clock clock_1 (.out(clock_1_out));
  D_Flip_Flop d_ff_1 (.D(Q0), .clk(clock_1_out), .Q(S0));  // open: Qn, preset, reset
  D_Flip_Flop d_ff_2 (.D(Q1), .clk(clock_1_out), .Q(S1));  // open: Qn, preset, reset
  D_Flip_Flop d_ff_3 (.D(Q2), .clk(clock_1_out), .Q(S2));  // open: Qn, preset, reset
  LedBar #(.matrixcols(3)) ledbar_1 (.led0(S2), .led1(S1), .led2(S0));
endmodule

module SemaforoProgramableE9 (
);

  wire and_1_out, and_2_out, and_3_out, and_4_out, and_5_out, Clear, Clock, or_1_out, Q0, Q1, Reset;
  wire [1:0] Estado;
  wire [3:0] Contador;
  wire [7:2] rom_1_data;

  Clock clock_1 (.out(Clock));
  and and_1 (and_1_out, Clock, Clear);
  Counter #(.max('hf), .width(4)) counter_1 (
    .Q(Contador), .clk(Clock), .clr(or_1_out));  // open: load, D, count, carry, up
  or or_1 (or_1_out, and_1_out, Reset);
  POR por_1 (.out(Reset));
  Hex_Digit_Display hex_digit_display_1 (.value(Contador));  // open: dp
  ROM #(.addrWidth(6), .misaligned("true")) rom_1 (.addr({Estado, Contador}), .data({rom_1_data, Q1, Q0}));
  D_Flip_Flop d_ff_1 (.D(Q0), .clk(Clock), .Q(Estado[0]));  // open: Qn, preset, reset
  D_Flip_Flop d_ff_2 (.D(Q1), .clk(Clock), .Q(Estado[1]));  // open: Qn, preset, reset
  LED led_1 (.in(rom_1_data[2]));
  LED led_2 (.in(rom_1_data[3]));
  LED led_3 (.in(rom_1_data[4]));
  LED led_4 (.in(rom_1_data[5]));
  LED led_5 (.in(rom_1_data[6]));
  LED led_6 (.in(rom_1_data[7]));
  and and_2 (and_2_out, Estado[0], ~Estado[1], ~Contador[0], ~Contador[1], Contador[2], Contador[3]);  // AND_Gate
  and and_3 (and_3_out, ~Estado[0], Estado[1], ~Contador[0], Contador[1], Contador[2], ~Contador[3]);  // AND_Gate
  and and_4 (and_4_out, Estado[0], Estado[1], ~Contador[0], Contador[1], Contador[2], Contador[3]);  // AND_Gate
  and and_5 (and_5_out, ~Estado[0], ~Estado[1], ~Contador[0], Contador[1], ~Contador[2], ~Contador[3]);  // AND_Gate
  or or_2 (Clear, and_2_out, and_3_out, and_4_out, and_5_out);

  // Other names for the same wires on the sheet: E0 = Contador[0]; E1 = Contador[1]; E2 = Contador[2];
  //   E3 = Contador[3]; S0 = Estado[0]; S1 = Estado[1]

  // Notes on the sheet:
  //   contents of rom_1 (hex, n*v repeats v):
  //   10*30 51 5*0 51 51 51 86 12*0 13*86 8b 0 0 8b 30
endmodule

module TecladoCajaFuerteE10 (
);

  wire D0, D1, D2, D3, D4, D5, D6, D7, D8, D9, DA;

  Button button_1 (.out(D7));
  Button button_2 (.out(D4));
  Button button_3 (.out(D1));
  Button button_4 (.out(D0));
  Button button_5 (.out(D8));
  Button button_6 (.out(D5));
  Button button_7 (.out(D2));
  Button button_8 (.out(DA));
  Button button_9 (.out(D9));
  Button button_10 (.out(D6));
  Button button_11 (.out(D3));
endmodule
